# Fritzing sketch ShotBotSchematicV4 (saved by Fritzing 0.9.4)
circuit board: 15cm x 10cm

parts:
  Part5 = Adafruit Feather M4 Express [part_number="Adafruit #3857"]
  S9 = Round Pushbutton
  LED7 = RGB LED (com. cathode, rgb) [package="5 mm [THT]"]
  JACK2 = 2.1mm Barrel Jack with Terminal Block
  M3 = DC Motor
  S10 = Taiway 100-SP-X-T1 SPDT Miniature Toggle Switch [part_number=100-SP-X-T1-0-0-B1-M2 package=THT]
  S11 = Taiway 100-SP-X-T1 SPDT Miniature Toggle Switch [part_number=100-SP-X-T1-0-0-B1-M2 package=THT]
  LED8 = Billie the Blue LED
  LED9 = Ruby the Red LED
  Part7 = VERTER 5V USB Buck-Boost
  M4 = Stepper Motor - Bipolar
  S13 = Square Pushbutton
  Part9 = Adafruit DC+Stepper FeatherWing [part_number="Adafruit #2927"]

nets (from the breadboard view):
  N1: Part5.D4, Part9.G
  N2: Part5.TX_D1, Part9.TX
  N3: Part5.RX_D0, Part9.RX
  N4: Part5.MISO, Part9.MISO
  N5: Part5.MOSI, Part9.MOSI
  N6: Part5.SCK, Part9.SCK
  N7: Part5.A5, Part9.F
  N8: Part5.A4, Part9.E
  N9: Part5.A3, Part9.D
  N10: Part5.A2, S13.leg0, Part9.C
  N11: Part5.A1, S9.leg0, Part9.B
  N12: Part5.A0, Part9.A
  GND: Part5.GND, JACK2.NEG, S10.L2, S11.L2, Part7.GND, Part9.GND
  N13: Part5.AREF, Part9.AREF
  +3V3: Part5.+3V3, S9.leg1, LED7.common_cathode, S10.COM, S13.leg1, Part9.+3.3V
  N14: Part5.!RESET, Part9.RESET
  N15: Part5.VBAT, Part9.VBAT
  N16: Part5.EN, Part9.EN
  N17: Part5.VBUS, Part9.USB
  N18: Part5.D13, Part9.N
  N19: Part5.D12, Part9.M
  N20: Part5.D11, LED7.red_anode, Part9.L
  N21: Part5.D10, LED7.green_anode, Part9.K
  N22: Part5.D9, LED7.blue_anode, Part9.J
  N23: Part5.D6, LED8.cathode, Part9.I
  N24: Part5.D5, Part9.H
  N25: Part5.SCL, Part9.SCL
  N26: Part5.SDA, Part9.SDA
  N27: JACK2.POS, S11.COM
  N28: M3.pin_1, Part9.M1A
  N29: M3.pin_2, Part9.M1B
  N30: S10.L1, LED8.anode
  N31: S11.L1, LED9.anode
  N32: LED9.cathode, Part7.VIN, Part9.VMOTOR
  N33: M4.A, Part9.M4A
  N34: M4.C, Part9.M4B
  N35: M4.B, Part9.M3B
  N36: M4.D, Part9.M3A

custom parts:
  Adafruit Feather M4 Express: It's what you've been waiting for, the Feather M4 Express featuring ATSAMD51. This Feather is fast like a swift, smart like an owl, strong like a ox-bird (it's half ox, half bird, OK?) This feather is powered by our new favorite chip, the ATSAMD51J19 - with its 120MHz Cortex M4 with floating point support and 512KB Flash and 192KB RAM. Your code will zig and zag and zoom, and with a bunch of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
  VERTER 5V USB Buck-Boost: VERTER can take battery voltages from 3-12VDC and output a nice 5V DC, which makes it a perfect universal power supply for your portable project! Where Verter really shines is when you have a battery or power range that can fluctuate a lot, or you don't know what you'll end up using.
  Adafruit DC+Stepper FeatherWing: This is the DC Motor + Stepper FeatherWing which will let you use 2 x bi-polar stepper motors or 4 x brushed DC motorx (or 1 stepper and 2 DC motors). Using our Feather Stacking Headers or Feather Female Headers you can connect a FeatherWing on top or bottom of your Feather board and let the board take flight! The original Adafruit Motorshield Kit is one of our most beloved kits, which is why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
